# Fritzing sketch at-me (saved by Fritzing 0.9.5d)
circuit board: 8.46667cm x 5.64444cm
breadboards: 2

parts:
  Arduino_Nano = Arduino Nano (Rev3.0)
  DFRobot_DFPlayer_Mini1 = DFRobot DFPlayer Mini [part_number=DFR0299]
  powerSwitch = Pushbutton [package="[THT]"]
  U2 = 3.5mm Audio Jack [package=audio-jack]
  R1 = Resistor [tolerance=±5% resistance=1k package=THT]
  LED1 = smd LED [color="Yellow (595nm)" package="1206 [SMD]"]
  R2 = Resistor [tolerance=±5% resistance=220 package=THT]
  Pads = Toggle Switch [package=THT]
  R3 = Resistor [tolerance=±5% resistance=10k package=THT]
  LED2 = LED - 5mm [color="Red (633nm)" package="5 mm [THT]"]
  R4 = Resistor [tolerance=±5% resistance=220 package=THT]
  shockDeliver = Pushbutton [package="[THT]"]
  R5 = Resistor [tolerance=±5% resistance=10k package=THT]

nets:
  N1: Arduino_Nano.GND, DFRobot_DFPlayer_Mini1.GND-1, DFRobot_DFPlayer_Mini1.GND-2, powerSwitch.Pin_1, powerSwitch.Pin_2, LED1.anode, R3.Pin_1, LED2.cathode, R5.Pin_0
  N2: Arduino_Nano.D2, R2.Pin_0
  N3: Arduino_Nano.D3, Pads.L1, R3.Pin_0
  N4: Arduino_Nano.D4, shockDeliver.Pin_3, shockDeliver.Pin_4, R5.Pin_1
  N5: Arduino_Nano.D5, R4.Pin_0
  N6: Arduino_Nano.D6, powerSwitch.Pin_3, powerSwitch.Pin_4
  N7: Arduino_Nano.D10, DFRobot_DFPlayer_Mini1.TX
  N8: Arduino_Nano.D11/MOSI, R1.Pin_1
  5V: Arduino_Nano.5V, DFRobot_DFPlayer_Mini1.VCC, Pads.COM, shockDeliver.Pin_1, shockDeliver.Pin_2
  N9: DFRobot_DFPlayer_Mini1.RX, R1.Pin_0
  N10: DFRobot_DFPlayer_Mini1.SPK_1, U2.LEFT
  N11: DFRobot_DFPlayer_Mini1.SPK_2, U2.RIGHT, U2.SLEEVE
  N12: LED1.cathode, R2.Pin_1
  N13: LED2.anode, R4.Pin_1
